# Fritzing sketch NeoPixel LED Controller (saved by Fritzing 0.9.4)
breadboards: 1

parts:
  WeMos_D1_Mini1 = WeMos D1 Mini
  5V = Power Jack [package=power_jack_pth]
  U1 = WS2812 RGB LED strip
  1000uF = Capacitor Polarized [package=cpol-radial-10uf-25v]

nets:
  5V: WeMos_D1_Mini1.5V, 5V.PWR, U1.VCC, 1000uF.+
  GND: WeMos_D1_Mini1.G, 5V.GND, U1.GND, 1000uF.-

custom parts:
  WS2812 RGB LED strip: WS2812 strip
